// Digital circuit Nibbler_01.dig as structural Verilog
module Nibbler_01 (
  input  U1,
  input  IN0,
  input  IN1,
  input  IN2,
  input  IN3,
  input  in_6,
  input  in_7,
  input  in_8,
  input  in_9
);

  wire A0, A1, A2, A3, ADR0, ADR1, ADR2, ADR3, ADR4, ADR5, ADR6, ADR7, ADR8, ADR9, ADR10, ADR11, ADR12,
       ADR13, ADR14, ADR15, CN_plus_4, D0, D1, D2, D3, D7, F0, F1, F2, F3, INCPC, INSTR0, INSTR1, INSTR2,
       INSTR3, M, nCARRYIN, nFLAGCARRY, nFLAGZERO, nLOADA, nLOADFLAGS, nLOADOUT, nLOADPC, nRES, nRST, nWERAM,
       OPRND0, OPRND1, OPRND2, OPRND3, or_3_out, or_4_out, OUT0, OUT1, OUT2, OUT3, OUT4, OUT5, OUT6, OUT7,
       P0, P1, P2, P3, P4, P5, P6, P7, Phase, RES, S0, S1, S2, S3, U2_pin8, U4_p15, U4_p16, U6_pin15,
       U7_pin15, U8_pin15, U13_pin14, U15_p29;

  PullUp pullup_1 (.out(IN3));
  PullUp pullup_2 (.out(nRST));
  Reset reset_1 (.out(nRST));
  PullUp pullup_3 (.out(IN2));
  PullUp pullup_4 (.out(IN1));
  PullUp pullup_5 (.out(IN0));
  _74163 U6 (
    .pin1(nRES), .pin2(U1), .pin3(P0), .pin4(P1), .pin5(P2), .pin6(P3), .pin7(1'b1), .pin8(1'b0),
    .pin9(nLOADPC), .pin10(INCPC), .pin11(ADR3), .pin12(ADR2), .pin13(ADR1), .pin14(ADR0), .pin15(U6_pin15),
    .pin16(1'b1));
  _74163 U7 (
    .pin1(nRES), .pin2(U1), .pin3(P4), .pin4(P5), .pin5(P6), .pin6(P7), .pin7(1'b1), .pin8(1'b0),
    .pin9(nLOADPC), .pin10(U6_pin15), .pin11(ADR7), .pin12(ADR6), .pin13(ADR5), .pin14(ADR4),
    .pin15(U7_pin15), .pin16(1'b1));
  _74163 U8 (
    .pin1(nRES), .pin2(U1), .pin3(OPRND0), .pin4(OPRND1), .pin5(OPRND2), .pin6(OPRND3), .pin7(1'b1),
    .pin8(1'b0), .pin9(nLOADPC), .pin10(U7_pin15), .pin11(ADR11), .pin12(ADR10), .pin13(ADR9), .pin14(ADR8),
    .pin15(U8_pin15), .pin16(1'b1));
  _74163 U9 (
    .pin1(nRES), .pin2(U1), .pin3(1'b0), .pin4(1'b0), .pin5(1'b0), .pin6(1'b0), .pin7(1'b0), .pin8(1'b0),
    .pin9(nLOADPC), .pin10(U8_pin15), .pin11(ADR15), .pin12(ADR14), .pin13(ADR13), .pin14(ADR12), .pin16(1'b1));  // open: pin15
  Seven_Seg_Hex seven_seg_hex_1 (.d(4'b0000), .dp(1'b0));
  Seven_Seg_Hex seven_seg_hex_2 (.d({OPRND3, OPRND2, OPRND1, OPRND0}), .dp(1'b0));
  // _28c256 U9_2: pin names not known; wires that end beside it: ADR14, ADR12, ADR7, ADR6, ADR5, ADR4, ADR3, ADR2, ADR1, ADR0, P0, 1'b1, 1'b1, ADR13, ADR8, ADR9, ADR11, 1'b0, ADR10, 1'b0, P7
  // _62256 U15: pin names not known; wires that end beside it: P1, P2, 1'b0, 1'b0, 1'b0, P7, P6, P5, P4, P3, P2, P1, P0, D0, D1, D2, 1'b0, P5, P4, P3, 1'b1, nWERAM, 1'b0, OPRND0, OPRND1, OPRND3, 1'b0, OPRND2, U15_p29, D7
  Seven_Seg_Hex seven_seg_hex_3 (.d({P7, P6, P5, P4}), .dp(1'b0));
  Seven_Seg_Hex seven_seg_hex_4 (.d({P3, P2, P1, P0}), .dp(1'b0));
  Seven_Seg_Hex seven_seg_hex_5 (.d({ADR15, ADR14, ADR13, ADR12}), .dp(1'b0));
  Seven_Seg_Hex seven_seg_hex_6 (.d({ADR11, ADR10, ADR9, ADR8}), .dp(1'b0));
  or or_1 (U15_p29, U1, in_8);
  Seven_Seg_Hex seven_seg_hex_7 (.d({ADR7, ADR6, ADR5, ADR4}), .dp(1'b0));
  _7474 U2 (
    .pin1(1'b1), .pin2(nRST), .pin3(U1), .pin4(1'b1), .pin5(nRES), .pin6(RES), .pin7(1'b0), .pin8(U2_pin8),
    .pin9(Phase), .pin10(1'b1), .pin11(U1), .pin12(U2_pin8), .pin13(nRES), .pin14(1'b1));
  _74125 U16 (
    .pin1(in_6), .pin2(IN0), .pin3(D0), .pin4(in_6), .pin5(IN1), .pin6(D1), .pin7(1'b0), .pin8(D2),
    .pin9(IN2), .pin10(in_6), .pin11(D3), .pin12(IN3), .pin13(in_6), .pin14(1'b1));
  Seven_Seg_Hex seven_seg_hex_8 (.d({ADR3, ADR2, ADR1, ADR0}), .dp(1'b0));
  Seven_Seg_Hex seven_seg_hex_9 (.d({D3, D2, D1, D0}), .dp(1'b0));
  _74377 U3 (
    .pin1(Phase), .pin2(OPRND0), .pin3(P0), .pin4(P1), .pin5(OPRND1), .pin6(OPRND2), .pin7(P2), .pin8(P3),
    .pin9(OPRND3), .pin10(1'b0), .pin11(U1), .pin12(INSTR0), .pin13(P4), .pin14(P5), .pin15(INSTR1),
    .pin16(INSTR2), .pin17(P6), .pin18(P7), .pin19(INSTR3), .pin20(1'b1));
  _74244 U14 (
    .pin1(in_7), .pin2(F0), .pin3(D3), .pin4(F1), .pin5(D2), .pin6(F2), .pin7(D1), .pin8(F3), .pin9(D0),
    .pin10(1'b0), .pin11(OPRND0), .pin12(D3), .pin13(OPRND1), .pin14(D2), .pin15(OPRND2), .pin16(D1),
    .pin17(OPRND3), .pin18(D0), .pin19(in_9), .pin20(1'b1));
  LED led_1 (.in(OUT7));
  LED led_2 (.in(OUT6));
  _74173 U13 (
    .pin1(1'b0), .pin2(1'b0), .pin3(nFLAGZERO), .pin4(nFLAGCARRY), .pin7(U1), .pin8(1'b0), .pin9(nLOADFLAGS),
    .pin10(nLOADFLAGS), .pin11(1'b0), .pin12(1'b0), .pin13(CN_plus_4), .pin14(U13_pin14), .pin15(1'b0),
    .pin16(1'b1));  // open: pin5, pin6
  _74173 U10 (
    .pin1(1'b0), .pin2(1'b0), .pin3(A0), .pin4(A1), .pin5(A2), .pin6(A3), .pin7(U1), .pin8(1'b0),
    .pin9(nLOADA), .pin10(nLOADA), .pin11(F3), .pin12(F2), .pin13(F1), .pin14(F0), .pin15(1'b0), .pin16(1'b1));
  _74173 U17 (
    .pin1(1'b0), .pin2(1'b0), .pin3(OUT0), .pin4(OUT1), .pin5(OUT2), .pin6(OUT3), .pin7(U1), .pin8(1'b0),
    .pin9(OPRND0), .pin10(nLOADOUT), .pin11(D3), .pin12(D2), .pin13(D1), .pin14(D0), .pin15(RES), .pin16(1'b1));
  LED led_3 (.in(OUT5));
  LED led_4 (.in(OUT4));
  LED led_5 (.in(OUT3));
  LED led_6 (.in(OUT2));
  LED led_7 (.in(OUT1));
  LED led_8 (.in(OUT0));
  or or_2 (U13_pin14, or_4_out, or_3_out);
  _74173 _74173_1 (
    .pin1(1'b0), .pin2(1'b0), .pin3(OUT4), .pin4(OUT5), .pin5(OUT6), .pin6(OUT7), .pin7(U1), .pin8(1'b0),
    .pin9(OPRND1), .pin10(nLOADOUT), .pin11(D3), .pin12(D2), .pin13(D1), .pin14(D0), .pin15(RES), .pin16(1'b1));
  or or_3 (or_3_out, F1, F0);
  or or_4 (or_4_out, F3, F2);
  // _27C1024 U4: pin names not known; wires that end beside it: 1'b1, 1'b0, INCPC, nLOADPC, nLOADA, nLOADFLAGS, nCARRYIN, M, S3, S2, 1'b0, S1, S0, nWERAM, U4_p15, U4_p16, 1'b1, D3, D2, D1, D0, A3, A2, A1
  _74181 U11 (
    .pin1(D0), .pin2(A0), .pin3(S3), .pin4(S2), .pin5(S1), .pin6(S0), .pin7(nCARRYIN), .pin8(M), .pin9(F0),
    .pin10(F1), .pin11(F2), .pin12(1'b0));  // open: pin13, pin14, pin15, pin16, pin17, pin18, pin19, pin20, pin21, pin22, pin23, pin24

  // Other names for the same wires on the sheet: CLK = U1; nOEALU = in_7; nOEIN = in_6; nOEOPRND = in_9;
  //   nOERAM = in_8

  // Notes on the sheet:
  //   U1: Hz: 2
  //   in_6: default 1
  //   in_8: default 1
  //   in_9: default 1
  //   "NIBBLER"
  //   PROGRAM COUNTER 0
  //   PROGRAM COUNTER 1
  //   PROGRAM COUNTER 2
  //   PROGRAM COUNTER 3
  //   SRAM ADDRESS
  //   PROGRAM ROM
  //   U12
  //   PC ADDRESS
  //   INPUT REG
  //   DATA
  //   INSTRUCTION REG
  //   DATA TO BUS
  //   FLAGS REG
  //   ACCUMULATOR
  //   OUTPUT REG 0
  //   DETECT ZERO
  //   OUTPUT REG 1
  //   uCODE ROM 0/ROM 1
  //   ALU
endmodule
